// Logisim project test_cpu.circ as structural Verilog: 1 circuit, main circuit main
module main (
  input  [15:0] in_1,
  output [15:0] out_2,
  output Done
);

  wire and_1_out, and_2_out, and_3_out, and_4_out, and_5_out, and_6_out, and_7_out, and_8_out, and_9_out,
       and_10_out, and_11_out, and_12_out, and_14_out, and_15_out, clock_1_out, decoder_1_out0,
       decoder_1_out1, decoder_1_out2, decoder_1_out3, decoder_2_out0, decoder_2_out1, decoder_2_out2,
       decoder_2_out3, decoder_3_out0, decoder_3_out1, decoder_3_out2, decoder_3_out3, decoder_3_out4,
       decoder_3_out5, or_3_out, or_4_out, or_5_out, or_7_out, or_8_out, or_9_out, or_12_out, or_13_out;
  wire [1:0] counter_1_q, multiplexer_1_out;
  wire [2:0] or_6_out, or_11_out;
  wire [5:0] register_1_q;
  wire [15:0] adder_1_out, multiplexer_3_out, register_2_q, register_3_q, register_4_q, register_5_q,
       register_6_q, register_7_q, subtractor_1_out;

  Clock clock_1 (.out(clock_1_out));
  Register #(.width(6)) register_1 (
    .D(in_1[15:10]), .en(decoder_2_out0), .Q(register_1_q), .clk(clock_1_out));  // open: clr
  or or_1 (or_6_out[2], and_4_out, and_12_out);
  Multiplexer #(.width(2), .enable("false")) multiplexer_1 (
    .in0(register_1_q[1:0]), .in1(register_1_q[3:2]), .out(multiplexer_1_out), .sel(and_10_out));
  Register #(.width(16)) register_2 (.D(out_2), .en(decoder_3_out0), .Q(register_2_q), .clk(clock_1_out));  // open: clr
  Register #(.width(16)) register_3 (.D(out_2), .en(decoder_3_out1), .Q(register_3_q), .clk(clock_1_out));  // open: clr
  Multiplexer #(.select(3), .width(16), .enable("false")) multiplexer_2 (
    .in0(register_2_q), .in1(register_3_q), .in2(register_4_q), .in3(register_5_q), .in4(in_1),
    .in5(register_7_q), .out(out_2), .sel(or_6_out));  // open: in6, in7
  or or_2 (or_6_out[1], and_2_out, and_1_out, and_3_out);
  and and_1 (and_1_out, and_10_out, multiplexer_1_out[1]);
  and and_2 (and_2_out, and_5_out, multiplexer_1_out[1]);
  Decoder #(.select(2), .enable("false")) decoder_1 (
    .out0(decoder_1_out0), .out1(decoder_1_out1), .out2(decoder_1_out2), .out3(decoder_1_out3),
    .sel(register_1_q[5:4]));
  Counter #(.width(2), .max('h3)) counter_1 (
    .Q(counter_1_q), .clk(clock_1_out), .clr(and_6_out));  // open: load, D, count, carry
  Decoder #(.select(2), .enable("false")) decoder_2 (
    .out0(decoder_2_out0), .out1(decoder_2_out1), .out2(decoder_2_out2), .out3(decoder_2_out3),
    .sel(counter_1_q));
  Register #(.width(16)) register_4 (.D(out_2), .en(decoder_3_out2), .Q(register_4_q), .clk(clock_1_out));  // open: clr
  and and_3 (and_3_out, and_11_out, multiplexer_1_out[1]);
  or or_3 (or_3_out, and_5_out, and_4_out);
  and and_4 (and_4_out, decoder_1_out1, decoder_2_out1);
  and and_5 (and_5_out, decoder_1_out0, decoder_2_out1);
  and and_6 (and_6_out, or_5_out, or_4_out);
  Register #(.width(16)) register_5 (.D(out_2), .en(decoder_3_out3), .Q(register_5_q), .clk(clock_1_out));  // open: clr
  and and_7 (and_7_out, and_10_out, multiplexer_1_out[0]);
  and and_8 (and_8_out, and_5_out, multiplexer_1_out[0]);
  or or_4 (or_4_out, decoder_1_out0, decoder_2_out1);
  or or_5 (or_5_out, decoder_2_out2, decoder_2_out2);
  or or_6 (or_6_out[0], and_8_out, and_7_out, and_9_out, and_12_out);
  and and_9 (and_9_out, and_11_out, multiplexer_1_out[0]);
  and and_10 (and_10_out, or_7_out, decoder_2_out1);
  or or_7 (or_7_out, decoder_1_out2, decoder_1_out3);
  and and_11 (and_11_out, or_9_out, decoder_2_out2);
  or or_8 (or_8_out, decoder_1_out2, decoder_1_out3);
  or or_9 (or_9_out, decoder_1_out2, decoder_1_out3);
  Decoder #(.select(3), .enable("false")) decoder_3 (
    .out0(decoder_3_out0), .out1(decoder_3_out1), .out2(decoder_3_out2), .out3(decoder_3_out3),
    .out4(decoder_3_out4), .out5(decoder_3_out5), .sel(or_11_out));  // open: out6, out7
  or or_10 (or_11_out[2], and_10_out, and_11_out);
  and and_12 (and_12_out, or_8_out, decoder_2_out3);
  or or_11 (or_11_out[0], and_11_out, and_15_out);
  and and_13 (or_11_out[1], register_1_q[3], or_12_out);
  or or_12 (or_12_out, or_3_out, and_12_out);
  and and_14 (and_14_out, decoder_1_out3, decoder_2_out2);
  Register #(.width(16)) register_6 (.D(out_2), .en(decoder_3_out4), .Q(register_6_q), .clk(clock_1_out));  // open: clr
  and and_15 (and_15_out, register_1_q[2], or_13_out);
  or or_13 (or_13_out, or_3_out, and_12_out);
  or or_14 (Done, and_12_out, or_3_out);
  Adder #(.width(16)) adder_1 (.a(out_2), .b(register_6_q), .out(adder_1_out));  // open: cin, cout
  Subtractor #(.width(16)) subtractor_1 (.a(register_6_q), .b(out_2), .out(subtractor_1_out));  // open: bin, bout
  Multiplexer #(.width(16), .enable("false")) multiplexer_3 (
    .in0(adder_1_out), .in1(subtractor_1_out), .out(multiplexer_3_out), .sel(and_14_out));
  Register #(.width(16)) register_7 (
    .D(multiplexer_3_out), .en(decoder_3_out5), .Q(register_7_q), .clk(clock_1_out));  // open: clr

  // Notes on the sheet:
  //   Clock
  //   DIN
  //   R0
  //   R1
  //   I0
  //   I
  //   T
  //   Clear
  //   R2
  //   R3
  //   I1
  //   T1
  //   T2
  //   T3
  //   A
  //   AddSub
  //   G
  //   BUS
endmodule
